# Fritzing sketch mbed_lpc1768_usb_host (saved by Fritzing 0.8.7b)
breadboards: 1

parts:
  Part1 = USB Type A Female Breakout Board [part_number=BOB-12700]  # not connected
  MBED1 = mbed
  R1 = Resistor [tolerance=±5% resistance=15k package=THT]
  R2 = Resistor [tolerance=±5% resistance=15k package=THT]

nets:
  N1: MBED1.GND, R1.Pin_1, R2.Pin_1
  N2: MBED1.D+, R1.Pin_0
  N3: MBED1.D-, R2.Pin_0

custom parts:
  USB Type A Female Breakout Board: USB breakout board for a Type A connector. sparkfun.com
